# Fritzing sketch Connections (saved by Fritzing 0.9.2b)
breadboards: 2

parts:
  M1 = Stepper Motor - Bipolar
  M2 = Stepper Motor - Bipolar
  M3 = Stepper Motor - Bipolar
  U1 = NodeMCU V1.0
  MD09B2 = A4988 Stepper Motor Driver Carrier
  MD09B3 = A4988 Stepper Motor Driver Carrier
  MD09B4 = A4988 Stepper Motor Driver Carrier
  Parte1 = Arduino Uno (Rev3)
  S1 = Toggle Switch [package=THT]
  R1 = Resistor [tolerance=±5% resistance=220 package=THT]
  R2 = Resistor [tolerance=±5% resistance=220 package=THT]
  S2 = Pushbutton [package="[THT]"]
  S3 = Pushbutton [package="[THT]"]
  S4 = Pushbutton [package="[THT]"]
  S5 = Pushbutton [package="[THT]"]
  S6 = Pushbutton [package="[THT]"]
  S7 = Pushbutton [package="[THT]"]
  R4 = Resistor [tolerance=±5% resistance=220 package=THT]
  R5 = Resistor [tolerance=±5% resistance=220 package=THT]
  R6 = Resistor [tolerance=±5% resistance=220 package=THT]
  R7 = Resistor [tolerance=±5% resistance=220 package=THT]
  R8 = Resistor [tolerance=±5% resistance=220 package=THT]
  R9 = Resistor [tolerance=±5% resistance=220 package=THT]
  Q1 = NPN-Transistor [package="TO92 [THT]"]
  Q2 = NPN-Transistor [package="TO92 [THT]"]
  Q3 = NPN-Transistor [package="TO92 [THT]"]
  Q4 = NPN-Transistor [package="TO92 [THT]"]
  R10 = Resistor [tolerance=±5% resistance=220 package=THT]
  R11 = Resistor [tolerance=±5% resistance=220 package=THT]
  R12 = Resistor [tolerance=±5% resistance=220 package=THT]
  R13 = Resistor [tolerance=±5% resistance=220 package=THT]
  C2 = Electrolytic Capacitor [capacitance=1µF package="100 mil [THT, electrolytic]"]
  LED1 = LED - 5mm [color="Red (633nm)" package="5 mm [THT]"]
  LED2 = LED - 5mm [color="Red (633nm)" package="5 mm [THT]"]

nets:
  N1: M1.A, MD09B2.OUT_2A
  N2: M1.C, MD09B2.OUT_2B
  N3: M1.B, MD09B2.OUT_1A
  N4: M1.D, MD09B2.OUT_1B
  N5: M2.A, MD09B3.OUT_2A
  N6: M2.C, MD09B3.OUT_2B
  N7: M2.B, MD09B3.OUT_1A
  N8: M2.D, MD09B3.OUT_1B
  N9: M3.A, MD09B4.OUT_2A
  N10: M3.C, MD09B4.OUT_2B
  N11: M3.B, MD09B4.OUT_1A
  N12: M3.D, MD09B4.OUT_1B
  N13: U1.D5, Parte1.A5/SCL
  N14: U1.D6, Parte1.A4/SDA
  N15: MD09B2.Enable, Parte1.D3_PWM
  N16: MD09B2.STEP, Parte1.D5_PWM
  N17: MD09B2.DIR, Parte1.D4
  N18: MD09B2.VMOT, MD09B3.VMOT, MD09B4.VMOT, C2.+
  N19: MD09B2.GROUND, MD09B3.GROUND, MD09B4.GROUND, Parte1.GND, S1.L2, R1.Pin_0, R2.Pin_0, R4.Pin_1, R5.Pin_1, R6.Pin_1, R7.Pin_1, R8.Pin_1, R9.Pin_1, C2.-
  VDD: MD09B2.VDD, MD09B3.VDD, MD09B4.VDD, Parte1.5V, S1.L1, S2.Pin_1, S2.Pin_2, S3.Pin_1, S3.Pin_2, S4.Pin_1, S4.Pin_2, S5.Pin_1, S5.Pin_2, S6.Pin_1, S6.Pin_2, S7.Pin_1, S7.Pin_2, Q1.C, Q2.C, Q3.C, Q4.C
  N20: MD09B3.Enable, Parte1.D6_PWM
  N21: MD09B3.RESET, MD09B3.SLEEP
  N22: MD09B3.STEP, Parte1.D8
  N23: MD09B3.DIR, Parte1.D7
  N24: MD09B4.Enable, Parte1.D9_PWM
  N25: MD09B4.STEP, Parte1.D11_PWM/MOSI
  N26: MD09B4.DIR, Parte1.D10_PWM/SS
  N27: Parte1.A0, S2.Pin_3, S2.Pin_4, R5.Pin_0, Q1.E
  N28: Parte1.A1, S3.Pin_3, S3.Pin_4, R4.Pin_0, Q2.E
  N29: Parte1.A2, S5.Pin_3, S5.Pin_4, R7.Pin_0, Q3.E
  N30: Parte1.A3, S6.Pin_3, S6.Pin_4, R8.Pin_0, Q4.E
  N31: Parte1.D12/MISO, LED1.anode
  N32: Parte1.D13/SCK, LED2.anode
  N33: Parte1.D2, S1.COM
  N34: R1.Pin_1, LED1.cathode
  N35: R2.Pin_1, LED2.cathode
  N36: S4.Pin_3, S4.Pin_4, R6.Pin_0, R11.Pin_1, R12.Pin_1
  N37: S7.Pin_3, S7.Pin_4, R9.Pin_0, R10.Pin_1, R13.Pin_1
  N38: Q1.B, R12.Pin_0
  N39: Q2.B, R11.Pin_0
  N40: Q3.B, R13.Pin_0
  N41: Q4.B, R10.Pin_0

notes:
  Voltage suppy

custom parts:
  NodeMCU V1.0: ESP8266 based NodeMCU

// code stored in the sketch: connectionsProyect.ino

